# Fritzing sketch sketch (saved by Fritzing 0.9.3b)
circuit board: 27.0127cm x 18.1062cm

parts:
  RTS_sender = ESP8266 NodeMCU LoLin module
  DS3231S(N)_RTC_and_Square_wave_generator = ZS-042 RTC Module
  (micro)SD_card_slot = microSD Socket [package=usd-socket-pp]
  Power_source_5-12V = DC Power [voltage=5]
  Master_device = ESP8266 NodeMCU LoLin module

nets:
  N1: RTS_sender.RX, Master_device.TX
  N2: RTS_sender.TX, Master_device.RX
  GND: RTS_sender.GND, DS3231S(N)_RTC_and_Square_wave_generator.GND, (micro)SD_card_slot.GND, Power_source_5-12V.V-, Master_device.GND
  VIN: RTS_sender.Vin, Power_source_5-12V.V+, Master_device.Vin
  VCC: DS3231S(N)_RTC_and_Square_wave_generator.VCC, (micro)SD_card_slot.VCC, Master_device.3V3
  N3: DS3231S(N)_RTC_and_Square_wave_generator.SDA, Master_device.D2
  N4: DS3231S(N)_RTC_and_Square_wave_generator.SCL, Master_device.D1
  N5: DS3231S(N)_RTC_and_Square_wave_generator.SQW, Master_device.D3
  N6: (micro)SD_card_slot.CS, Master_device.D8
  N7: (micro)SD_card_slot.DI, Master_device.D7
  N8: (micro)SD_card_slot.SCK, Master_device.D5
  N9: (micro)SD_card_slot.DO, Master_device.D6

custom parts:
  ESP8266 NodeMCU LoLin module: ESP8266 based NodeMCU
